// Logisim project ex5.circ as structural Verilog: 5 circuits, main circuit rotr
module rotr (
  input  [15:0] A,
  input  [3:0] B,
  output [15:0] Out1
);

  Multiplexer #(.select(4), .width(16), .enable("false")) multiplexer_1 (
    .in0(A), .in1({A[14:0], A[15]}), .in2({A[13:0], A[15:14]}), .in3({A[12:0], A[15:13]}),
    .in4({A[11:0], A[15:12]}), .in5({A[10:0], A[15:11]}), .in6({A[9:0], A[15:10]}), .in7({A[8:0], A[15:9]}),
    .in8({A[7:0], A[15:8]}), .in9({A[6:0], A[15:7]}), .in10({A[5:0], A[15:6]}), .in11({A[4:0], A[15:5]}),
    .in12({A[3:0], A[15:4]}), .in13({A[2:0], A[15:3]}), .in14({A[1:0], A[15:2]}), .in15(A), .out(Out1),
    .sel(B));

  // Notes on the sheet:
  //   PUT CIRCUITRY HERE
endmodule

module rot8 (
  input  [15:0] in_1,
  output [15:0] out_2
);


  // Notes on the sheet:
  //   PUT CIRCUITRY HERE
endmodule

module rot4 (
  input  [15:0] in_1,
  output [15:0] out_2
);


  // Notes on the sheet:
  //   PUT CIRCUITRY HERE
endmodule

module rot2 (
  input  [15:0] in_1,
  output [15:0] out_2
);


  // Notes on the sheet:
  //   PUT CIRCUITRY HERE
endmodule

module rot1 (
  input  [15:0] in_1,
  output [15:0] out_2
);


  // Notes on the sheet:
  //   PUT CIRCUITRY HERE
endmodule
